# Fritzing sketch early diagnosis schematic (saved by Fritzing 0.9.3b)
breadboards: 1

parts:
  Part1 = Arduino Due (Rev2b)
  Part2 = Arduino Pro Mini v13
  LCD1 = LCD screen
  X1 = USB Connectors [package=usb-a-s-silk-female]
  CONN1 = USB connector [package=THT]
  X2 = USB Connectors [package=usb-a-s-silk-female]
  X4 = USB Connectors [package=usb-a-s-silk-female]
  LCM1602_IIC2 = LCM1602 IIC [part_number="LCM1602 IIC" chip_label="LCM1602 IIC" package="DIP (Dual Inline) [THT]"]
  J1 = Basic Force Sensing Resistor (FSR) [package=THT]
  Part5 = Arduino Pro Mini v13
  CONN3 = USB connector [package=THT]
  C1 = Ceramic Capacitor [capacitance="100 nF" package="1206 [SMD, multilayer]"]
  Part6 = SHT1x-Breakout
  Part7 = Arduino Pro Mini v13
  CONN4 = USB connector [package=THT]

nets:
  N1: Part1.D14/TX3, X1.D+
  N2: Part1.D15/RX3, X1.D-
  N3: Part1.D16/TX2, X2.D+
  N4: Part1.D17/RX2, X2.D-
  N5: Part1.D18/TX1, X4.D+
  N6: Part1.D19/RX1, X4.D-
  N7: Part1.D20/SDA3, LCM1602_IIC2.SDA
  N8: Part1.D21/SCL3, LCM1602_IIC2.SCL
  GND: Part1.GND, X1.GND, X2.GND, X4.GND, LCM1602_IIC2.GND
  5V: Part1.5V, X1.VBUS, X2.VBUS, X4.VBUS, LCM1602_IIC2.VCC
  N9: Part2.D0/TX, CONN3.d+
  N10: Part2.D1/RX, CONN3.d-
  N11: Part2.GND, CONN3.chassis5, CONN3.chassis6
  VCC: Part2.VCC, CONN3.5V, C1.1
  N12: Part2.A0, C1.0
  VSS: LCD1.VSS, LCM1602_IIC2.VSS
  VDD: LCD1.VDD, LCM1602_IIC2.VDD
  N13: LCD1.V0, LCM1602_IIC2.V0
  N14: LCD1.RS, LCM1602_IIC2.RS
  N15: LCD1.R/W, LCM1602_IIC2.RW
  N16: LCD1.E, LCM1602_IIC2.E
  N17: LCD1.DB0, LCM1602_IIC2.D0
  N18: LCD1.DB1, LCM1602_IIC2.D1
  N19: LCD1.DB2, LCM1602_IIC2.D2
  N20: LCD1.DB3, LCM1602_IIC2.D3
  N21: LCD1.DB4, LCM1602_IIC2.D4
  N22: LCD1.DB5, LCM1602_IIC2.D5
  N23: LCD1.DB6, LCM1602_IIC2.D6
  N24: LCD1.DB7, LCM1602_IIC2.D7
  N25: LCD1.LED+, LCM1602_IIC2.A
  N26: LCD1.LED-, LCM1602_IIC2.K
  5V_2: CONN1.5V, Part5.VCC
  N27: CONN1.d-, Part5.D1/RX
  N28: CONN1.d+, Part5.D0/TX
  N29: CONN1.chassis5, CONN1.chassis6, J1.pin_1, Part5.GND
  N30: LCM1602_IIC2.LED_A, LCM1602_IIC2.LED_B
  N31: J1.pin_0, Part5.A0
  N32: Part6.SCK, Part7.A5
  N33: Part6.DATA, Part7.A4
  VCC_2: Part6.VCC, Part7.VCC, CONN4.5V
  GND_2: Part6.GND, Part7.GND, CONN4.GND, CONN4.chassis5, CONN4.chassis6
  N34: Part7.D0/TX, CONN4.d+
  N35: Part7.D1/RX, CONN4.d-

notes:
  Treating as MAX30100 chip

custom parts:
  LCM1602 IIC: I2C-Module to use a 1602 or 2004 LCD on with the wire.h libory Serial LCD Modul
